// Logisim project processador_monocilo.circ as structural Verilog: 12 circuits, main circuit mips
module mips (
  input  ResetPC,
  input  ResetRegs,
  input  in_3
);

  wire alu_1_out_5, and_1_out, control_unit_1_alusrc, control_unit_1_branch, control_unit_1_jump,
       control_unit_1_memtoreg, control_unit_1_memw, control_unit_1_regdst, control_unit_1_regw;
  wire [1:0] control_unit_1_aluop;
  wire [2:0] alu_control_1_out_3;
  wire [4:0] mem_inst_1_inst_15_11, mem_inst_1_inst_20_16, mem_inst_1_inst_25_21, multiplexer_1_out;
  wire [5:0] mem_inst_1_inst_5_0, mem_inst_1_inst_31_26;
  wire [15:0] mem_inst_1_inst_15_0;
  wire [31:0] alu_1_ula_r, mem_dados_1_out_5, mem_inst_1_out_3, multiplexer_2_out, multiplexer_3_out,
       pc_control_1_pc, regs_1_readdata1_2, regs_1_readdata2, sign_extensor_1_inst32bit;

  mem_inst mem_inst_1 (
    .PC(pc_control_1_pc), .out_3(mem_inst_1_out_3), .Inst_31_26(mem_inst_1_inst_31_26),
    .Inst_25_21(mem_inst_1_inst_25_21), .Inst_20_16(mem_inst_1_inst_20_16),
    .Inst_15_11(mem_inst_1_inst_15_11), .Inst_15_0(mem_inst_1_inst_15_0), .Inst_5_0(mem_inst_1_inst_5_0),
    .in_2(in_3));
  // Probe on mem_inst_1_inst_25_21
  // Probe on mem_inst_1_inst_20_16
  // Probe on mem_inst_1_inst_15_11
  // Probe on mem_inst_1_inst_5_0
  control_unit control_unit_1 (
    .Inst31_26(mem_inst_1_inst_31_26), .RegDst(control_unit_1_regdst), .RegW(control_unit_1_regw),
    .ALUOp(control_unit_1_aluop), .MemToReg(control_unit_1_memtoreg), .ALUSrc(control_unit_1_alusrc),
    .MemW(control_unit_1_memw), .Branch(control_unit_1_branch), .Jump(control_unit_1_jump));  // open: MemR
  Multiplexer #(.width(5), .enable("false")) multiplexer_1 (
    .in0(mem_inst_1_inst_20_16), .in1(mem_inst_1_inst_15_11), .out(multiplexer_1_out),
    .sel(control_unit_1_regdst));
  regs regs_1 (
    .RegW(control_unit_1_regw), .ReadData1(mem_inst_1_inst_25_21), .ReadReg2(mem_inst_1_inst_20_16),
    .WriteData(multiplexer_3_out), .ReadData1_2(regs_1_readdata1_2), .ReadData2(regs_1_readdata2),
    .WriteReg(multiplexer_1_out), .in_6(ResetRegs), .in_7(in_3));
  sign_extensor sign_extensor_1 (.Inst_15_0(mem_inst_1_inst_15_0), .Inst32bit(sign_extensor_1_inst32bit));
  Multiplexer #(.width(32), .enable("false")) multiplexer_2 (
    .in0(regs_1_readdata2), .in1(sign_extensor_1_inst32bit), .out(multiplexer_2_out),
    .sel(control_unit_1_alusrc));
  // Probe on control_unit_1_aluop
  // Probe on multiplexer_2_out
  alu_control alu_control_1 (.in_1(control_unit_1_aluop), .in_2(mem_inst_1_inst_5_0), .out_3(alu_control_1_out_3));
  and and_1 (and_1_out, control_unit_1_branch, alu_1_out_5);
  // Probe on alu_control_1_out_3
  alu alu_1 (
    .out_5(alu_1_out_5), .in_1(regs_1_readdata1_2), .in_3(multiplexer_2_out), .in_2(alu_control_1_out_3),
    .ULA_R(alu_1_ula_r));
  // Probe on alu_1_out_5
  // Probe on multiplexer_3_out
  // Probe on alu_1_ula_r
  PC_control pc_control_1 (
    .ZB(and_1_out), .InstAtual(mem_inst_1_out_3), .PC(pc_control_1_pc), .clk(in_3), .reset(ResetPC),
    .J(control_unit_1_jump));
  // Probe on pc_control_1_pc
  // Probe on mem_inst_1_out_3
  mem_dados mem_dados_1 (
    .ALUResult(alu_1_ula_r), .in_4(in_3), .in_3(regs_1_readdata2), .out_5(mem_dados_1_out_5),
    .MemW(control_unit_1_memw));
  Multiplexer #(.width(32), .enable("false")) multiplexer_3 (
    .in0(alu_1_ula_r), .in1(mem_dados_1_out_5), .out(multiplexer_3_out), .sel(control_unit_1_memtoreg));
endmodule

// ALU
module alu (
  input  [31:0] in_1,
  input  [2:0] in_2,
  input  [31:0] in_3,
  output [31:0] ULA_R,
  output out_5
);

  wire or_2_out;
  wire [31:0] adder_1_out, and_1_out, or_1_out, subtractor_1_out;

  Multiplier multiplier_1 ();  // open: a, b, out, cin, cout
  Adder #(.width(32)) adder_1 (.a(in_1), .b(in_3), .out(adder_1_out));  // open: cin, cout
  Subtractor #(.width(32)) subtractor_1 (.a(in_1), .b(in_3), .out(subtractor_1_out));  // open: bin, bout
  assign and_1_out = in_1 & in_3;  // AND_Gate and_1, 32 bits wide
  assign or_1_out = in_1 | in_3;  // OR_Gate or_1, 32 bits wide
  Multiplexer #(.select(3), .width(32), .enable("false")) multiplexer_1 (
    .in0(adder_1_out), .in1(subtractor_1_out), .in2(adder_1_out), .in3(and_1_out), .in4(or_1_out),
    .in5(subtractor_1_out), .in6(or_1_out), .in7(and_1_out), .out(ULA_R), .sel(in_2));
  not not_1 (out_5, or_2_out);
  or or_2 (or_2_out, ULA_R[0], ULA_R[1], ULA_R[2], ULA_R[3], ULA_R[4], ULA_R[5], ULA_R[6], ULA_R[7], ULA_R[8], ULA_R[9], ULA_R[10], ULA_R[11], ULA_R[12], ULA_R[13], ULA_R[14], ULA_R[15], ULA_R[16], ULA_R[17], ULA_R[18], ULA_R[19], ULA_R[20], ULA_R[21], ULA_R[22], ULA_R[23], ULA_R[24], ULA_R[25], ULA_R[26], ULA_R[27], ULA_R[28], ULA_R[29], ULA_R[30], ULA_R[31]);
endmodule

// ALUControl
module alu_control (
  input  [1:0] in_1,
  input  [5:0] in_2,
  output [2:0] out_3
);

  wire add_out, beq_out, ls_out, rformat_out, sub_out;
  wire [2:0] and_2_out, and_3_out, and_4_out, and_5_out, and_6_out;
  wire [2:2] and_out, mult_out, or_2_out, or_3_out, or_out;

  and add (add_out, rformat_out, ~in_2[0], ~in_2[1], ~in_2[2], ~in_2[4], ~in_2[4], in_2[5]);  // AND_Gate
  and sub (sub_out, rformat_out, ~in_2[0], in_2[1], ~in_2[2], ~in_2[4], ~in_2[4], in_2[5]);  // AND_Gate
  and mult (mult_out[2], rformat_out, ~in_2[0], ~in_2[1], ~in_2[2], in_2[4], in_2[4], ~in_2[5]);  // AND_Gate
  and \and  (and_out[2], rformat_out, ~in_2[0], ~in_2[1], in_2[2], ~in_2[4], ~in_2[4], in_2[5]);  // AND_Gate
  and \or  (or_out[2], rformat_out, in_2[0], ~in_2[1], in_2[2], ~in_2[4], ~in_2[4], in_2[5]);  // AND_Gate
  and rformat (rformat_out, ~in_1[0], in_1[1]);  // AND_Gate
  and ls (ls_out, ~in_1[0], ~in_1[1]);  // AND_Gate
  and beq (beq_out, in_1[0], ~in_1[1]);  // AND_Gate
  or or_2 (or_2_out[2], ls_out, add_out);
  or or_3 (or_3_out[2], beq_out, sub_out);
  // Probe on 3'b000
  // Probe on {3{or_2_out[2]}}
  // Probe on {3{or_3_out[2]}}
  assign and_2_out = 3'b011 & {3{and_out[2]}};  // AND_Gate and_2, 3 bits wide
  assign and_3_out = 3'b100 & {3{or_out[2]}};  // AND_Gate and_3, 3 bits wide
  // Probe on 3'b001
  // Probe on and_4_out
  assign and_4_out = 3'b000 & {3{or_2_out[2]}};  // AND_Gate and_4, 3 bits wide
  assign and_5_out = 3'b001 & {3{or_3_out[2]}};  // AND_Gate and_5, 3 bits wide
  assign and_6_out = 3'b010 & {3{mult_out[2]}};  // AND_Gate and_6, 3 bits wide
  assign out_3 = and_4_out | and_5_out | and_6_out | and_2_out | and_3_out;  // OR_Gate or_4, 3 bits wide

  assign in_2[3] = in_2[4];
endmodule

// ControlUnit
module control_unit (
  input  [5:0] Inst31_26,
  output RegDst,
  output RegW,
  output [1:0] ALUOp,
  output MemToReg,
  output MemR,
  output ALUSrc,
  output MemW,
  output Branch,
  output Jump
);

  and rformat (ALUOp[1], ~Inst31_26[0], ~Inst31_26[1], ~Inst31_26[2], ~Inst31_26[3], ~Inst31_26[4], ~Inst31_26[5]);  // AND_Gate
  and lw (MemR, Inst31_26[0], ~Inst31_26[1], ~Inst31_26[2], ~Inst31_26[3], Inst31_26[4], Inst31_26[5]);  // AND_Gate
  and sw (MemW, Inst31_26[0], ~Inst31_26[1], Inst31_26[2], ~Inst31_26[3], Inst31_26[4], Inst31_26[5]);  // AND_Gate
  and beq (ALUOp[0], ~Inst31_26[0], ~Inst31_26[1], ~Inst31_26[2], Inst31_26[3], ~Inst31_26[4], ~Inst31_26[5]);  // AND_Gate
  and u_jump (Jump, ~Inst31_26[0], ~Inst31_26[1], ~Inst31_26[2], ~Inst31_26[3], Inst31_26[4], ~Inst31_26[5]);  // AND_Gate
  or or_1 (RegW, ALUOp[1], MemR);
  or or_2 (ALUSrc, MemR, MemW);

  assign Branch = ALUOp[0];
  assign MemToReg = MemR;
  assign RegDst = ALUOp[1];
endmodule

// DataMem
module mem_dados (
  input  [31:0] ALUResult,
  input  MemW,
  input  [31:0] in_3,
  input  in_4,
  output [31:0] out_5
);

  wire [31:0] rom_1_data;

  ROM #(.addrWidth(24), .dataWidth(32)) rom_1 (.addr(ALUResult[23:0]), .data(rom_1_data));
  // Probe on ALUResult[23:0]
  RAM #(.addrWidth(24), .dataWidth(32), .trigger("high"), .databus("bibus")) ram_1 (
    .addr(ALUResult[23:0]), .we(1'b0), .oe(in_4), .dout(out_5));  // open: din
  // Probe on rom_1_data
  RAM #(.addrWidth(24), .dataWidth(32), .trigger("high"), .databus("bibus")) ram_2 (
    .addr(ALUResult[23:0]), .we(MemW), .oe(1'b0), .din(in_3));  // open: dout

  assign ALUResult[30:24] = {7{ALUResult[31]}};
  // also tied to GND on the sheet: ALUResult[31]

  // Notes on the sheet:
  //   Memoria de dados ROM nao implementada
endmodule

// Regs
module regs (
  input  RegW,
  input  [4:0] ReadData1,
  input  [4:0] ReadReg2,
  input  [4:0] WriteReg,
  input  [31:0] WriteData,
  input  in_6,
  input  in_7,
  output [31:0] ReadData1_2,
  output [31:0] ReadData2
);

  wire and_1_out, and_2_out, and_3_out, and_4_out, and_5_out, and_6_out, and_7_out, and_8_out, and_9_out,
       and_10_out, and_11_out, and_12_out, and_13_out, and_14_out, and_15_out, and_16_out, and_17_out,
       and_18_out, and_19_out, and_20_out, and_21_out, and_22_out, and_23_out, and_24_out, and_25_out,
       and_26_out, and_27_out, and_28_out, and_29_out, and_30_out, and_31_out, and_32_out, decoder_1_out0,
       decoder_1_out1, decoder_1_out2, decoder_1_out3, decoder_1_out4, decoder_1_out5, decoder_1_out6,
       decoder_1_out7, decoder_1_out8, decoder_1_out9, decoder_1_out10, decoder_1_out11, decoder_1_out12,
       decoder_1_out13, decoder_1_out14, decoder_1_out15, decoder_1_out16, decoder_1_out17, decoder_1_out18,
       decoder_1_out19, decoder_1_out20, decoder_1_out21, decoder_1_out22, decoder_1_out23, decoder_1_out24,
       decoder_1_out25, decoder_1_out26, decoder_1_out27, decoder_1_out28, decoder_1_out29, decoder_1_out30,
       decoder_1_out31, decoder_2_out0, decoder_2_out1;
  wire [31:0] R0_2_q, R1_q, R2_2_q, R3_2_q, R4_q, register_1_q, register_2_q, register_3_q, register_4_q,
       register_5_q, register_6_q, register_7_q, register_8_q, register_9_q, register_10_q, register_11_q,
       register_12_q, register_13_q, register_14_q, register_15_q, register_16_q, register_17_q,
       register_18_q, register_19_q, register_20_q, register_21_q, register_22_q, register_23_q,
       register_24_q, register_25_q, register_26_q, register_27_q, undriven;

  Decoder #(.select(5), .enable("false")) decoder_1 (
    .out0(decoder_1_out0), .out1(decoder_1_out1), .out2(decoder_1_out2), .out3(decoder_1_out3),
    .out4(decoder_1_out4), .out5(decoder_1_out5), .out6(decoder_1_out6), .out7(decoder_1_out7),
    .out8(decoder_1_out8), .out9(decoder_1_out9), .out10(decoder_1_out10), .out11(decoder_1_out11),
    .out12(decoder_1_out12), .out13(decoder_1_out13), .out14(decoder_1_out14), .out15(decoder_1_out15),
    .out16(decoder_1_out16), .out17(decoder_1_out17), .out18(decoder_1_out18), .out19(decoder_1_out19),
    .out20(decoder_1_out20), .out21(decoder_1_out21), .out22(decoder_1_out22), .out23(decoder_1_out23),
    .out24(decoder_1_out24), .out25(decoder_1_out25), .out26(decoder_1_out26), .out27(decoder_1_out27),
    .out28(decoder_1_out28), .out29(decoder_1_out29), .out30(decoder_1_out30), .out31(decoder_1_out31),
    .sel(WriteReg));
  Decoder #(.enable("false")) decoder_2 (.out0(decoder_2_out0), .out1(decoder_2_out1), .sel(RegW));
  // Probe on R0_2_q
  Register #(.width(32)) R0_2 (.D(WriteData), .en(and_1_out), .clk(in_7), .Q(R0_2_q), .clr(in_6));
  and and_1 (and_1_out, decoder_1_out0, decoder_2_out1);
  Register #(.width(32)) register_1 (.D(WriteData), .en(and_2_out), .clk(in_7), .Q(register_1_q));  // open: clr
  and and_2 (and_2_out, decoder_1_out8, decoder_2_out1);
  Register #(.width(32)) register_2 (.D(WriteData), .en(and_3_out), .clk(in_7), .Q(register_2_q));  // open: clr
  and and_3 (and_3_out, decoder_1_out16, decoder_2_out1);
  Register #(.width(32)) register_3 (.D(undriven), .en(and_4_out), .clk(in_7), .Q(register_3_q));  // open: clr
  and and_4 (and_4_out, decoder_1_out24, decoder_2_out1);
  Register #(.width(32)) R1 (.D(WriteData), .en(and_5_out), .clk(in_7), .Q(R1_q), .clr(in_6));
  and and_5 (and_5_out, decoder_1_out1, decoder_2_out1);
  Register #(.width(32)) register_4 (.D(WriteData), .en(and_6_out), .clk(in_7), .Q(register_4_q));  // open: clr
  and and_6 (and_6_out, decoder_1_out9, decoder_2_out1);
  Register #(.width(32)) register_5 (.D(WriteData), .en(and_7_out), .clk(in_7), .Q(register_5_q));  // open: clr
  and and_7 (and_7_out, decoder_1_out17, decoder_2_out1);
  Register #(.width(32)) register_6 (.D(undriven), .en(and_8_out), .clk(in_7), .Q(register_6_q));  // open: clr
  and and_8 (and_8_out, decoder_1_out25, decoder_2_out1);
  // Probe on R1_q
  and and_9 (and_9_out, decoder_1_out2, decoder_2_out1);
  and and_10 (and_10_out, decoder_1_out10, decoder_2_out1);
  and and_11 (and_11_out, decoder_1_out18, decoder_2_out1);
  Register #(.width(32)) register_7 (.D(undriven), .en(and_12_out), .clk(in_7), .Q(register_7_q));  // open: clr
  and and_12 (and_12_out, decoder_1_out26, decoder_2_out1);
  // Probe on R2_2_q
  Register #(.width(32), .trigger("falling")) R2_2 (.D(WriteData), .en(and_9_out), .clk(in_7), .Q(R2_2_q), .clr(in_6));
  Register #(.width(32)) register_8 (.D(WriteData), .en(and_10_out), .clk(in_7), .Q(register_8_q));  // open: clr
  Register #(.width(32)) register_9 (.D(WriteData), .en(and_11_out), .clk(in_7), .Q(register_9_q));  // open: clr
  and and_13 (and_13_out, decoder_1_out27, decoder_2_out1);
  // Probe on R3_2_q
  Register #(.width(32), .trigger("falling")) R3_2 (.D(WriteData), .en(and_14_out), .clk(in_7), .Q(R3_2_q), .clr(in_6));
  and and_14 (and_14_out, decoder_1_out3, decoder_2_out1);
  Register #(.width(32)) register_10 (.D(WriteData), .en(and_15_out), .clk(in_7), .Q(register_10_q));  // open: clr
  and and_15 (and_15_out, decoder_1_out11, decoder_2_out1);
  Register #(.width(32)) register_11 (.D(WriteData), .en(and_16_out), .clk(in_7), .Q(register_11_q));  // open: clr
  and and_16 (and_16_out, decoder_1_out19, decoder_2_out1);
  Register #(.width(32)) register_12 (.D(undriven), .en(and_13_out), .clk(in_7), .Q(register_12_q));  // open: clr
  Register #(.width(32), .trigger("falling")) R4 (.D(WriteData), .en(and_17_out), .clk(in_7), .Q(R4_q), .clr(in_6));
  and and_17 (and_17_out, decoder_1_out4, decoder_2_out1);
  Register #(.width(32)) register_13 (.D(WriteData), .en(and_18_out), .clk(in_7), .Q(register_13_q));  // open: clr
  and and_18 (and_18_out, decoder_1_out12, decoder_2_out1);
  Register #(.width(32)) register_14 (.D(WriteData), .en(and_19_out), .clk(in_7), .Q(register_14_q));  // open: clr
  and and_19 (and_19_out, decoder_1_out20, decoder_2_out1);
  Register #(.width(32)) register_15 (.D(undriven), .en(and_20_out), .clk(in_7), .Q(register_15_q));  // open: clr
  and and_20 (and_20_out, decoder_1_out28, decoder_2_out1);
  // Probe on R4_q
  and and_21 (and_21_out, decoder_1_out5, decoder_2_out1);
  Register #(.width(32)) register_16 (.D(WriteData), .en(and_22_out), .clk(in_7), .Q(register_16_q));  // open: clr
  and and_22 (and_22_out, decoder_1_out13, decoder_2_out1);
  Register #(.width(32)) register_17 (.D(WriteData), .en(and_23_out), .clk(in_7), .Q(register_17_q));  // open: clr
  and and_23 (and_23_out, decoder_1_out21, decoder_2_out1);
  Register #(.width(32)) register_18 (.D(undriven), .en(and_24_out), .clk(in_7), .Q(register_18_q));  // open: clr
  and and_24 (and_24_out, decoder_1_out29, decoder_2_out1);
  Register #(.width(32)) register_19 (.D(WriteData), .en(and_21_out), .clk(in_7), .Q(register_19_q));  // open: clr
  and and_25 (and_25_out, decoder_1_out30, decoder_2_out1);
  Register #(.width(32)) register_20 (.D(WriteData), .en(and_26_out), .clk(in_7), .Q(register_20_q));  // open: clr
  and and_26 (and_26_out, decoder_1_out6, decoder_2_out1);
  Register #(.width(32)) register_21 (.D(WriteData), .en(and_27_out), .clk(in_7), .Q(register_21_q));  // open: clr
  and and_27 (and_27_out, decoder_1_out14, decoder_2_out1);
  Register #(.width(32)) register_22 (.D(WriteData), .en(and_28_out), .clk(in_7), .Q(register_22_q));  // open: clr
  and and_28 (and_28_out, decoder_1_out22, decoder_2_out1);
  Register #(.width(32)) register_23 (.D(undriven), .en(and_25_out), .clk(in_7), .Q(register_23_q));  // open: clr
  Register #(.width(32)) register_24 (.D(WriteData), .en(and_29_out), .clk(in_7), .Q(register_24_q));  // open: clr
  and and_29 (and_29_out, decoder_1_out7, decoder_2_out1);
  Register #(.width(32)) register_25 (.D(WriteData), .en(and_30_out), .clk(in_7), .Q(register_25_q));  // open: clr
  and and_30 (and_30_out, decoder_1_out15, decoder_2_out1);
  Register #(.width(32)) register_26 (.D(WriteData), .en(and_31_out), .clk(in_7), .Q(register_26_q));  // open: clr
  and and_31 (and_31_out, decoder_1_out23, decoder_2_out1);
  Register #(.width(32)) register_27 (.D(undriven), .en(and_32_out), .clk(in_7), .Q(register_27_q));  // open: clr
  and and_32 (and_32_out, decoder_1_out31, decoder_2_out1);
  Multiplexer #(.select(5), .width(32), .enable("false")) multiplexer_1 (
    .in0(R0_2_q), .in1(R1_q), .in2(R2_2_q), .in3(R3_2_q), .in4(R4_q), .in5(register_19_q),
    .in6(register_20_q), .in7(register_24_q), .in8(register_1_q), .in9(register_4_q), .in10(register_8_q),
    .in11(register_10_q), .in12(register_13_q), .in13(register_16_q), .in14(register_21_q),
    .in15(register_25_q), .in16(register_2_q), .in17(register_5_q), .in18(register_9_q),
    .in19(register_11_q), .in20(register_14_q), .in21(register_17_q), .in22(register_22_q),
    .in23(register_26_q), .in24(register_3_q), .in25(register_6_q), .in26(register_7_q),
    .in27(register_12_q), .in28(register_15_q), .in29(register_18_q), .in30(register_23_q),
    .in31(register_27_q), .out(ReadData1_2), .sel(ReadData1));
  Multiplexer #(.select(5), .width(32), .enable("false")) multiplexer_2 (
    .in0(R0_2_q), .in1(R1_q), .in2(R2_2_q), .in3(R3_2_q), .in4(R4_q), .in5(register_19_q),
    .in6(register_20_q), .in7(register_24_q), .in8(register_1_q), .in9(register_4_q), .in10(register_8_q),
    .in11(register_10_q), .in12(register_13_q), .in13(register_16_q), .in14(register_21_q),
    .in15(register_25_q), .in16(register_2_q), .in17(register_5_q), .in18(register_9_q),
    .in19(register_11_q), .in20(register_14_q), .in21(register_17_q), .in22(register_22_q),
    .in23(register_26_q), .in24(register_3_q), .in25(register_6_q), .in26(register_7_q),
    .in27(register_12_q), .in28(register_15_q), .in29(register_18_q), .in30(register_23_q),
    .in31(register_27_q), .out(ReadData2), .sel(ReadReg2));
endmodule

// SignEx
module sign_extensor (
  input  [15:0] Inst_15_0,
  output [31:0] Inst32bit
);


  assign Inst32bit = {{17{Inst_15_0[15]}}, Inst_15_0[14:0]};
endmodule

// PCControl
module PC_control (
  input  [31:0] InstAtual,
  input  ZB,
  input  J,
  input  clk,
  input  reset,
  output [31:0] PC
);

  wire [31:0] adder_1_out, multiplexer_1_out, multiplexer_2_out;

  Register #(.width(32), .trigger("falling")) register_1 (
    .D(multiplexer_2_out), .en(1'b1), .clk(clk), .Q(PC), .clr(reset));
  Adder #(.width(32)) adder_1 (.a(32'h1), .b(PC), .out(adder_1_out));  // open: cin, cout
  // Probe on InstAtual
  // Probe on adder_1_out
  Multiplexer #(.width(32), .enable("false")) multiplexer_1 (
    .in0(adder_1_out), .in1({{16{1'b0}}, InstAtual[15:0]}), .out(multiplexer_1_out), .sel(ZB));
  Multiplexer #(.width(32), .enable("false")) multiplexer_2 (
    .in0(multiplexer_1_out), .in1({{16{1'b0}}, InstAtual[15:0]}), .out(multiplexer_2_out), .sel(J));
endmodule

module separa_inst (
  input  [31:0] Inst_31_0,
  output [5:0] Inst_31_26,
  output [4:0] Inst_25_21,
  output [4:0] Inst_20_16,
  output [4:0] Inst_15_11,
  output [15:0] Inst_15_0,
  output [5:0] Inst_5_0
);


  assign Inst_5_0 = Inst_31_0[5:0];
  assign Inst_15_0 = Inst_31_0[15:0];
  assign Inst_15_11 = Inst_31_0[15:11];
  assign Inst_20_16 = Inst_31_0[20:16];
  assign Inst_25_21 = Inst_31_0[25:21];
  assign Inst_31_26 = Inst_31_0[31:26];
endmodule

// InstMem
module mem_inst (
  input  [31:0] PC,
  input  in_2,
  output [31:0] out_3,
  output [5:0] Inst_31_26,
  output [4:0] Inst_25_21,
  output [4:0] Inst_20_16,
  output [4:0] Inst_15_11,
  output [15:0] Inst_15_0,
  output [5:0] Inst_5_0
);

  wire [31:0] rom_1_data;

  ROM #(.addrWidth(24), .dataWidth(32)) rom_1 (.addr(PC[23:0]), .data(rom_1_data));
  RAM #(.addrWidth(24), .dataWidth(32), .databus("bibus")) ram_1 (
    .addr(PC[23:0]), .we(1'b0), .oe(in_2), .clk(in_2), .dout(out_3));  // open: din
  // Probe on rom_1_data
  separa_inst separa_inst_1 (
    .Inst_31_0(out_3), .Inst_31_26(Inst_31_26), .Inst_25_21(Inst_25_21), .Inst_20_16(Inst_20_16),
    .Inst_15_11(Inst_15_11), .Inst_15_0(Inst_15_0), .Inst_5_0(Inst_5_0));

  assign PC[30:24] = {7{PC[31]}};
  // also tied to GND on the sheet: PC[31]

  // Notes on the sheet:
  //   contents of rom_1 (hex, n*v repeats v):
  //   c4020000 c4030001 432020 20830005 431024 40000002
endmodule

module rom (
);

  ROM rom_1 ();  // open: addr, data
  RAM ram_1 ();  // open: addr, data, sel, clk, ld, clr
endmodule

module main (
  input  in_1
);

  wire clock_1_out;

  Clock clock_1 (.out(clock_1_out));
  mips mips_1 (.ResetRegs(in_1), .ResetPC(in_1), .in_3(clock_1_out));
endmodule
